# Fritzing sketch computer-power-supply (saved by Fritzing 0.9.3b)
breadboards: 1

parts:
  D2 = Rectifier Diode [part_number=1N4001 package="300 mil [THT]"]
  D1 = Rectifier Diode [part_number=1N4001 package="300 mil [THT]"]
  V1 = AC Power
  F1 = Resettable Fuse PTC [package=0603]
  C1 = Electrolytic Capacitor [capacitance=100µF package="300 mil [THT, electrolytic]"]

nets:
  GND: D2.cathode, C1.-
  Possible issue with diodes connected in series: D2.anode, D1.cathode, C1.+
  N1: D1.anode, F1.2
  N2: V1.V-, F1.1

custom parts:
  AC Power: A generic ac power symbol
  Resettable Fuse PTC: Resettable Fuse PTC Resettable Fuse. Spark Fun Electronics SKU : COM-08357
